// Logisim project DSD Final Project.circ as structural Verilog: 4 circuits, main circuit ALU
module ALU (
  input  [7:0] Rx,
  input  [7:0] Ry,
  input  Asen,
  output [7:0] Result
);

  wire [7:0] adder_1_out, subtractor_1_out;

  Adder adder_1 (.a(Rx), .b(Ry), .out(adder_1_out));  // open: cin, cout
  Subtractor subtractor_1 (.a(Rx), .b(Ry), .out(subtractor_1_out));  // open: bin, bout
  Multiplexer #(.width(8), .enable("false")) multiplexer_1 (
    .in0(adder_1_out), .in1(subtractor_1_out), .out(Result), .sel(Asen));
endmodule

module Counter (
  input  Clock,
  input  Clear,
  output MSB,
  output LSB
);

  wire and_1_out, and_2_out, d_ff_2_qn, not_1_out, xor_1_out;

  and and_1 (and_1_out, not_1_out, xor_1_out);
  xor xor_1 (xor_1_out, LSB, MSB);
  not not_1 (not_1_out, Clear);
  D_Flip_Flop d_ff_1 (.clk(Clock), .D(and_1_out), .Q(MSB));  // open: Qn, preset, en, reset
  and and_2 (and_2_out, not_1_out, d_ff_2_qn);
  D_Flip_Flop d_ff_2 (.clk(Clock), .D(and_2_out), .Q(LSB), .Qn(d_ff_2_qn));  // open: preset, en, reset
endmodule

module Control (
  input  Reset,
  input  [7:0] in_2,
  input  LSB,
  input  MSB,
  output R0,
  output R1,
  output R2,
  output R3,
  output R4,
  output R5,
  output R6,
  output R7,
  output Done,
  output Clear,
  output Ain,
  output Asen,
  output Bin,
  output Bout,
  output IRin,
  output DIN_Out,
  output [2:0] Rout
);

  wire and_1_out, and_2_out, and_5_out, decoder_1_out1, not_1_out, not_2_out, not_3_out, or_1_out;
  wire [2:0] controlled_buffer_1_out, controlled_buffer_2_out;

  Decoder #(.select(2)) decoder_1 (
    .out0(IRin), .out1(decoder_1_out1), .out2(Bin), .out3(Bout), .sel({MSB, LSB}));  // open: en
  Demultiplexer #(.select(3)) demultiplexer_1 (
    .out0(R0), .out1(R1), .out2(R2), .out3(R3), .out4(R4), .out5(R5), .out6(R6), .out7(R7), .in(Done),
    .sel(in_2[5:3]));  // open: en
  not not_1 (not_1_out, in_2[7]);
  not not_2 (not_2_out, in_2[7]);
  and and_1 (and_1_out, not_2_out, decoder_1_out1);
  and and_2 (and_2_out, Bout, in_2[7]);
  and and_3 (Ain, decoder_1_out1, in_2[7]);
  and and_4 (Asen, Bin, in_2[6]);
  not not_3 (not_3_out, in_2[7]);
  assign controlled_buffer_1_out = Ain ? in_2[5:3] : 3'bz;  // Controlled_Buffer controlled_buffer_1
  assign controlled_buffer_2_out = or_1_out ? in_2[2:0] : 3'bz;  // Controlled_Buffer controlled_buffer_2
  or or_1 (or_1_out, and_5_out, Bin);
  and and_5 (and_5_out, not_1_out, decoder_1_out1);
  or or_2 (Done, and_1_out, and_2_out);
  and and_6 (DIN_Out, not_3_out, in_2[6]);
  Multiplexer #(.width(3)) multiplexer_1 (
    .in0(controlled_buffer_1_out), .in1(controlled_buffer_2_out), .out(Rout), .sel(or_1_out));  // open: en
  or or_3 (Clear, Done, Reset);
endmodule

module CPU (
  input  Reset,
  input  Reset_RAM
);

  wire and_1_out, clock_1_out, control_1_ain, control_1_asen, control_1_bin, control_1_clear, control_1_irin,
       control_1_r0, control_1_r1, control_1_r2, control_1_r3, control_1_r4, control_1_r5, control_1_r6,
       control_1_r7, counter_2_lsb, counter_2_msb;
  wire [1:0] control_1_bout;
  wire [2:0] control_1_rout;
  wire [3:0] _1_q, _1_q_2, _5_q, _5_q_2, _6_q, _6_q_2, counter_1_q;
  wire [7:0] _0_q, _2_q, _3_q, _4_q, _7_q, A_q, alu_1_result, B_q, IR_q, multiplexer_1_out,
       multiplexer_2_out, multiplexer_3_out, multiplexer_4_out, ram_1_data;

  Clock clock_1 (.out(clock_1_out));
  Register _0 (.D(multiplexer_4_out), .en(control_1_r0), .Q(_0_q), .clk(clock_1_out));  // open: clr
  Register _1 (.D(multiplexer_4_out), .en(control_1_r1), .Q({_1_q_2, _1_q}), .clk(clock_1_out));  // open: clr
  Register _2 (.D(multiplexer_4_out), .en(control_1_r2), .Q(_2_q), .clk(clock_1_out));  // open: clr
  Register _3 (.D(multiplexer_4_out), .en(control_1_r3), .Q(_3_q), .clk(clock_1_out));  // open: clr
  Register _4 (.D(multiplexer_4_out), .en(control_1_r4), .Q(_4_q), .clk(clock_1_out));  // open: clr
  Register _5 (.D(multiplexer_4_out), .en(control_1_r5), .Q({_5_q_2, _5_q}), .clk(clock_1_out));  // open: clr
  Register _6 (.D(multiplexer_4_out), .en(control_1_r6), .Q({_6_q_2, _6_q}), .clk(clock_1_out));  // open: clr
  Register _7 (.D(multiplexer_4_out), .en(control_1_r7), .Q(_7_q), .clk(clock_1_out));  // open: clr
  Hex_Digit_Display hex_digit_display_1 (.value(_0_q[7:4]));  // open: dp
  Multiplexer #(.select(3), .width(8), .enable("false")) multiplexer_1 (
    .in0(_0_q), .in1({_1_q_2, _1_q}), .in2(_2_q), .in3(_3_q), .in4(_4_q), .in5({_5_q_2, _5_q}),
    .in6({_6_q_2, _6_q}), .in7(_7_q), .out(multiplexer_1_out), .sel(control_1_rout));
  Hex_Digit_Display hex_digit_display_2 (.value(_1_q_2));  // open: dp
  Hex_Digit_Display hex_digit_display_3 (.value(_0_q[3:0]));  // open: dp
  Hex_Digit_Display hex_digit_display_4 (.value(_1_q));  // open: dp
  Multiplexer #(.width(8)) multiplexer_2 (
    .in1(ram_1_data), .out(multiplexer_2_out), .sel(control_1_bout[1]));  // open: in0, en
  Multiplexer #(.width(8)) multiplexer_3 (
    .in1(B_q), .out(multiplexer_3_out), .sel(control_1_bout[0]));  // open: in0, en
  Counter_part #(.width(4), .max('hf)) counter_1 (
    .Q(counter_1_q), .clk(and_1_out), .clr(Reset_RAM));  // open: load, D, count, carry
  Hex_Digit_Display hex_digit_display_5 (.value(_2_q[3:0]));  // open: dp
  Hex_Digit_Display hex_digit_display_6 (.value(_2_q[7:4]));  // open: dp
  Register A (.D(multiplexer_4_out), .en(control_1_ain), .Q(A_q), .clk(clock_1_out));  // open: clr
  Hex_Digit_Display hex_digit_display_7 (.value(_3_q[7:4]));  // open: dp
  ALU alu_1 (.Rx(A_q), .Ry(multiplexer_4_out), .Asen(control_1_asen), .Result(alu_1_result));
  RAM #(.addrWidth(4), .bus("asynch")) ram_1 (
    .addr(counter_1_q), .data(ram_1_data), .ld(1'b1), .clr(Reset_RAM));  // open: sel
  and and_1 (and_1_out, control_1_irin, clock_1_out);
  Hex_Digit_Display hex_digit_display_8 (.value(_3_q[3:0]));  // open: dp
  Multiplexer #(.select(2), .width(8)) multiplexer_4 (
    .in0(multiplexer_1_out), .in1(multiplexer_3_out), .in2(multiplexer_2_out), .out(multiplexer_4_out),
    .sel(control_1_bout));  // open: in3, en
  Register IR (.D(ram_1_data), .en(control_1_irin), .Q(IR_q), .clk(clock_1_out));  // open: clr
  Hex_Digit_Display hex_digit_display_9 (.value(_4_q[7:4]));  // open: dp
  Hex_Digit_Display hex_digit_display_10 (.value(_4_q[3:0]));  // open: dp
  Register B (.D(alu_1_result), .en(control_1_bin), .Q(B_q), .clk(clock_1_out));  // open: clr
  Hex_Digit_Display hex_digit_display_11 (.value(_5_q_2));  // open: dp
  Hex_Digit_Display hex_digit_display_12 (.value(_5_q));  // open: dp
  Hex_Digit_Display hex_digit_display_13 (.value(_6_q_2));  // open: dp
  Hex_Digit_Display hex_digit_display_14 (.value(_6_q));  // open: dp
  Hex_Digit_Display hex_digit_display_15 (.value(_7_q[7:4]));  // open: dp
  Hex_Digit_Display hex_digit_display_16 (.value(_7_q[3:0]));  // open: dp
  Control control_1 (
    .Reset(Reset), .in_2(IR_q), .LSB(counter_2_lsb), .MSB(counter_2_msb), .Clear(control_1_clear),
    .Ain(control_1_ain), .Asen(control_1_asen), .Bin(control_1_bin), .Bout(control_1_bout[0]),
    .IRin(control_1_irin), .DIN_Out(control_1_bout[1]), .Rout(control_1_rout), .R0(control_1_r0),
    .R1(control_1_r1), .R2(control_1_r2), .R3(control_1_r3), .R4(control_1_r4), .R5(control_1_r5),
    .R6(control_1_r6), .R7(control_1_r7));  // open: Done
  Counter counter_2 (.Clock(clock_1_out), .Clear(control_1_clear), .MSB(counter_2_msb), .LSB(counter_2_lsb));

  // Notes on the sheet:
  //   R0
  //   R1
  //   R2
  //   R3
  //   R4
  //   R5
  //   R6
  //   R7
endmodule
